// Logisim project CPU_v2.circ as structural Verilog: 5 circuits, main circuit main
module main (
);

  wire clock_1_out, clock_3_out, clock_4_out, clock_5_out, clock_6_out, clock_7_out, dipswitch_1_sw8,
       en_write, not_1_out, not_2_out, op2_is_imm, por_1_out, R, ram_in, ram_ope, small_rd, writeback_alu;
  wire [0:0] clock_2_out;
  wire [1:0] dipswitch_1_sw2, ldiCode, multiplexer_2_out, PcMode;
  wire [3:0] RA2, WA_RA1;
  wire [4:0] AluOp;
  wire [5:0] register_1_q;
  wire [6:5] pla_2_out;
  wire [7:0] ALU_Result, Immediate, R0, R1, R2, R3, R4, R5, R6, ram_1_dout, RD1, RD2, RD2_out, RD3,
       RegFileInput, rom_1_data;
  wire [15:0] PcReg;

  POR por_1 (.out(por_1_out));
  Clock clock_1 (.out(clock_1_out));
  // Probe on R0
  // Probe on R1
  // Probe on R2
  // Probe on R3
  // Probe on R4
  // Probe on R5
  // Probe on R6
  // Probe on {R1, R0}
  // Probe on {R3, R2}
  // Probe on {R5, R4}
  // Probe on {R2, R1, R0}
  // Probe on {R5, R4, R3}
  D_Flip_Flop d_ff_1 (.D(por_1_out), .clk(clock_1_out), .Q(R), .preset(por_1_out));  // open: Qn, reset
  // Probe on nothing
  // Probe on R0
  // Probe on R1
  // Probe on R2
  // Probe on R3
  // Probe on R4
  // Probe on R5
  // Probe on R6
  // Probe on {R1, R0}
  // Probe on {R3, R2}
  // Probe on {R5, R4}
  // Probe on {R2, R1, R0}
  // Probe on {R5, R4, R3}
  assign RD2_out = not_1_out ? RD2 : 8'bz;  // Controlled_Buffer controlled_buffer_1
  not not_1 (not_1_out, op2_is_imm);
  assign RD2_out = op2_is_imm ? Immediate : 8'bz;  // Controlled_Buffer controlled_buffer_2
  DipSwitch dipswitch_1 (
    .sw1(dipswitch_1_sw2[1]), .sw2(dipswitch_1_sw2[0]), .sw8(dipswitch_1_sw8));  // open: sw3, sw4, sw5, sw6, sw7
  Clock clock_2 (.out(clock_2_out[0]));
  LedBar ledbar_1 (
    .led0(RegFileInput[7]), .led1(RegFileInput[6]), .led2(RegFileInput[5]), .led3(RegFileInput[4]),
    .led4(RegFileInput[3]), .led5(RegFileInput[2]), .led6(RegFileInput[1]), .led7(RegFileInput[0]));
  Multiplexer #(.width(8)) multiplexer_1 (.in0(RD2_out), .in1(ALU_Result), .out(RegFileInput), .sel(writeback_alu));
  ROM #(.addrWidth(16)) rom_1 (.addr({PcReg[15:1], clock_2_out[0]}), .data({rom_1_data[7:6], RA2, rom_1_data[1:0]}));
  Multiplexer #(.width(2)) multiplexer_2 (
    .in0(PcMode), .in1(dipswitch_1_sw2), .out(multiplexer_2_out), .sel(dipswitch_1_sw8));
  Clock clock_3 (.out(clock_3_out));
  Clock clock_4 (.out(clock_4_out));
  Clock clock_5 (.out(clock_5_out));
  Clock clock_6 (.out(clock_6_out));
  RAM #(.addrWidth(16), .enables("line")) ram_1 (
    .addr({RD3, RD2}), .we(ram_in), .clk(clock_6_out), .din(RD1), .dout(ram_1_dout));
  LedBar ledbar_2 (
    .led0(RD1[7]), .led1(RD1[6]), .led2(RD1[5]), .led3(RD1[4]), .led4(RD1[3]), .led5(RD1[2]), .led6(RD1[1]),
    .led7(RD1[0]));
  Clock clock_7 (.out(clock_7_out));
  RegisterFile registerfile_1 (
    .EnableWrite(en_write), .Write(WA_RA1[2:0]), .WriteData(RegFileInput), .PortA(WA_RA1[2:0]),
    .PortB(RA2[2:0]), .clk(clock_4_out), .R(R), .RD1(RD1), .RD2(RD2), .RD3(RD3), .R6_out(R6), .R5_out(R5),
    .R4_out(R4), .R3_out(R3), .R2_out(R2), .R1_out(R1), .R0_out(R0));
  ALU alu_1 (
    .AluOp(AluOp), .Enable(writeback_alu), .RD1(RD1), .RD2(RD2), .clk(clock_5_out), .R(R), .Result(ALU_Result));
  Register #(.trigger("high")) register_1 (
    .D({rom_1_data[7:6], RA2, rom_1_data[1:0]}), .clk(clock_7_out), .Q({WA_RA1[1:0], register_1_q}));  // open: en, clr
  ProgramCounter programcounter_1 (
    .RelativeAddr(RD2_out), .AbisoluteAddr({RD3, RD2}), .CounterMode(multiplexer_2_out), .clk(clock_3_out),
    .Reset(R), .PC(PcReg));
  LedBar ledbar_3 (
    .led0(RD2_out[7]), .led1(RD2_out[6]), .led2(RD2_out[5]), .led3(RD2_out[4]), .led4(RD2_out[3]),
    .led5(RD2_out[2]), .led6(RD2_out[1]), .led7(RD2_out[0]));
  not not_2 (not_2_out, ram_ope);
  LedBar ledbar_4 (
    .led0(RD3[7]), .led1(RD3[6]), .led2(RD3[5]), .led3(RD3[4]), .led4(RD3[3]), .led5(RD3[2]), .led6(RD3[1]),
    .led7(RD3[0]));
  PLA #(.in_width(6), .out_width(10), .\table ("000000 0000000000\n000001 0001110000\n000010 0000100000\n000011 0101000000\n000100 0100000000\n000101 1000000000\n000110 0010100000\n000111 0010100000\n001000 0010100000\n001001 0010100000\n001010 0010100000\n001011 0010100000\n001100 0010100000\n001101 0010100000\n001110 0010100000\n001111 0010100000\n010000 0010100000\n010001 0010100000\n010010 0010100000\n010011 0010100000\n010100 0010000000\n010101 0010000000\n010110 0010100000\n010111 0001110100\n011000 0001111000\n011001 0001111100\n011010 0000000000\n011011 0000000000\n011100 0001100000\n011101 0001100000\n011110 0001100010\n011111 0000000001\n100000 0010100000\n100001 0010100000\n100010 0010100000\n100011 0010100000\n100100 0010100000\n100101 0010100000\n100110 0010100000\n100111 0010100000\n101000 0010100000\n101001 0010100000\n101010 0010100000\n101011 0010100000\n101100 0010100000\n101101 0010100000\n101110 0010100000\n101111 0010100000\n110000 0000000000\n110001 0000000000\n110010 0000000000\n110011 0000000000\n110100 0000000000\n110101 0000000000\n110110 0000000000\n110111 0000000000\n111000 0000000000\n111001 0000000000\n111010 0000000000\n111011 0000000000\n111100 0000000000\n111101 0000000000\n111110 0000000000\n111111 0000000000")) pla_1 (
    .in(register_1_q), .out({PcMode, writeback_alu, op2_is_imm, en_write, small_rd, ldiCode, ram_ope, ram_in}));
  PLA #(.in_width(6), .out_width(7), .\table ("000000 0000000\n000001 0000000\n000010 0000000\n000011 0000000\n000100 0000000\n000101 0000000\n000110 0000000\n000111 0000001\n001000 0000010\n001001 0000011\n001010 0000100\n001011 0000101\n001100 0000110\n001101 0000111\n001110 0001000\n001111 0001001\n010000 0001010\n010001 0001101\n010010 0001110\n010011 0001111\n010100 0000010\n010101 0001101\n010110 0001100\n010111 0000000\n011000 0000000\n011001 0000000\n011010 0000000\n011011 0000000\n011100 0100000\n011101 1000000\n011110 0000000\n011111 0000000\n100000 0010000\n100001 0010001\n100010 0010010\n100011 0010011\n100100 0010100\n100101 0010101\n100110 0010110\n100111 0010111\n101000 0011000\n101001 0011001\n101010 0011010\n101011 0011011\n101100 0011100\n101101 0011101\n101110 0011110\n101111 0011111\n110000 0000000\n110001 0000000\n110010 0000000\n110011 0000000\n110100 0000000\n110101 0000000\n110110 0000000\n110111 0000000\n111000 0000000\n111001 0000000\n111010 0000000\n111011 0000000\n111100 0000000\n111101 0000000\n111110 0000000\n111111 0000000")) pla_2 (
    .in(register_1_q), .out({pla_2_out, AluOp}));
  assign Immediate = not_2_out ? {rom_1_data[7:6], RA2, rom_1_data[1:0]} : 8'bz;  // Controlled_Buffer controlled_buffer_3
  assign Immediate = ram_ope ? ram_1_dout : 8'bz;  // Controlled_Buffer controlled_buffer_4
  Multiplexer #(.width(2)) multiplexer_3 (.in0(rom_1_data[1:0]), .in1(ldiCode), .out(WA_RA1[3:2]), .sel(small_rd));

  // Other names for the same wires on the sheet: RD32[15:0] = {RD3, RD2}

  // Notes on the sheet:
  //   contents of rom_1 (hex, n*v repeats v):
  //   0 41 5 2 5 82 5 c2 55 41 55 81 8 48 1 c1 4 55 10 e4 d c6 1 c1 d 86 aa 41 5 42 aa 81 14 42 8 48 1 c1
  //   4 55 10 e4 d c6 1 c1 d 86 7e 41 4 82 4 88 8 42 1 c1 4 55 10 e4 d c6 1 c1 d 86 a 41 14 81 8 46 1e 81
  //   8 48 1 c1 4 55 10 e4 d c6 1 c1 d 86 32 41 14 81 8 48 1e 81 8 48 1 c1 4 55 10 e4 d c6 1 c1 d 86 ff 41
  //   1 81 8 46 0 41 0 81 8 47 1 81 8 48 1 c1 4 55 10 e4 d c6 1 c1 d 86 0 41 1 81 8 48 a 41 5 81 8 49 4 81
  //   8 48 1 c1 4 55 10 e4 d c6 1 c1 d 86 aa 41 0 4a 55 81 8 48 1 c1 4 55 10 e4 d c6 1 c1 d 86 1 41 0 4b
  //   ff 81 8 48 1 c1 4 55 10 e4 d c6 1 c1 d 86 1 41 0 4c 2 81 8 48 1 c1 4 55 10 e4 d c6 1 c1 d 86 4 41 0
  //   4e 2 81 8 48 1 c1 4 55 10 e4 d c6 1 c1 d 86 80 41 0 50 c0 81 8 48 1 c1 4 55 10 e4 d c6 1 c1 d 86 ff
  //   41 1 81 8 46 1 41 0 4d 3 81 8 48 1 c1 4 55 10 e4 d c6 1 c1 d 86 ff 41 1 81 8 46 2 41 0 4f 81 81 8 48
  //   1 c1 4 55 10 e4 d c6 1 c1 d 86 ff 41 f 81 8 51 8 48 1 c1 4 55 10 e4 d c6 1 c1 d 86 f0 41 f 81 8 52
  //   ff 81 8 48 1 c1 4 55 10 e4 d c6 1 c1 d 86 ff 41 55 81 8 53 aa 81 8 48 1 c1 4 55 10 e4 d c6 1 c1 d 86
  //   5 41 5 81 8 54 1 41 10 64 1 c1 4 55 10 e4 d c6 1 c1 d 86 5 41 3 81 8 54 1 41 10 65 1 c1 4 55 10 e4 d
  //   c6 1 c1 d 86 f0 41 f 81 8 55 1 41 10 64 1 c1 4 55 10 e4 d c6 1 c1 d 86 ff 41 1 81 8 46 1 41 10 62 1
  //   c1 4 55 10 e4 d c6 1 c1 d 86 1 41 1 81 8 46 1 41 10 63 1 c1 4 55 10 e4 d c6 1 c1 d 86 80 41 0 81 8
  //   46 1 41 10 66 1 c1 4 55 10 e4 d c6 1 c1 d 86 7f 41 0 81 8 46 1 41 10 67 1 c1 4 55 10 e4 d c6 1 c1 d
  //   86 7f 41 1 81 8 46 1 41 10 68 1 c1 4 55 10 e4 d c6 1 c1 d 86 1 41 1 81 8 46 1 41 10 69 1 c1 4 55 10
  //   e4 d c6 1 c1 d 86 0 3 1 41 10 60 1 c1 4 55 10 e4 d c6 1 c1 d 86 0 41 1 81 8 61 1 c1 4 55 10 e4 d c6
  //   1 c1 d 86 a 41 5 81 8 54 1 41 10 62 1 c1 4 55 10 e4 d c6 1 c1 d 86 3 41 a 81 8 54 1 41 10 63 1 c1 4
  //   55 10 e4 d c6 1 c1 d 86 5 41 5 81 8 54 1 41 10 6a 1 c1 4 55 10 e4 d c6 1 c1 d 86 a 41 5 81 8 54 1 41
  //   10 6b 1 c1 4 55 10 e4 d c6 1 c1 d 86 5 41 3 81 8 54 1 41 10 6d 1 c1 4 55 10 e4 d c6 1 c1 d 86 ff 41
  //   1 81 8 54 1 41 10 6c 1 c1 4 55 10 e4 d c6 1 c1 d 86 3 41 3 81 8 54 1 41 10 6e 1 c1 4 55 10 e4 d c6 1
  //   c1 d 86 5 41 3 81 8 54 1 41 10 6f 1 c1 4 55 10 e4 d c6 1 c1 d 86 ff 41 5 42 0 41 4 54 1 56 1 56 1 41
  //   10 64 1 c1 4 55 10 e4 d c6 1 c1 d 86 0 41 4 54 ab 41 0 81 f0 c1 8 5f 0 41 8 5e ab 81 8 48 1 c1 4 55
  //   10 e4 d c6 1 c1 d 86 cd 41 2 81 f0 c1 8 5f 0 41 0 81 f0 c1 8 5e ab 81 8 48 1 c1 4 55 10 e4 d c6 1 c1
  //   d 86 0 5c 0 9d 76 57 3 97 4 c2 14 c8 0 41 c 65 1 c1 4 55 10 e4 d c6 1 c1 d 86 0 41 4 3 1 41 1 c1 4
  //   55 10 e4 d c6 1 c1 d 86 4 41 5 42 0 41 14 4 1 41 1 c1 4 55 10 e4 d c6 1 c1 d 86 0 41 c4 81 3 c1 8 5
  //   1 41 1 c1 4 55 10 e4 d c6 1 c1 d 86 0 41 6*0 1 c1 4 55 10 e4 d c6 1 c1 d 86 0 3
endmodule

module PLA_Decoder_LOp (
  input  [3:0] LOp,
  input  [3:0] RD2,
  input  [3:0] RD1,
  output Swap,
  output [3:0] result
);

  PLA #(.in_width(12), .out_width(1), .\table ("xxxxxxxx1111 1")) pla_1 (.in({RD1, RD2, LOp}), .out(Swap));
  PLA #(.in_width(12), .out_width(1), .\table ("xxx0xxx0xxx1 1\nxxx0xxx1xx1x 1\nxxx1xxx0x1xx 1\nxxx1xxx11xxx 1")) pla_2 (
    .in({RD1, RD2, LOp}), .out(result[0]));
  PLA #(.in_width(12), .out_width(1), .\table ("xx0xxx0xxxx1 1\nxx0xxx1xxx1x 1\nxx1xxx0xx1xx 1\nxx1xxx1x1xxx 1")) pla_3 (
    .in({RD1, RD2, LOp}), .out(result[1]));
  PLA #(.in_width(12), .out_width(1), .\table ("x0xxx0xxxxx1 1\nx0xxx1xxxx1x 1\nx1xxx0xxx1xx 1\nx1xxx1xx1xxx 1")) pla_4 (
    .in({RD1, RD2, LOp}), .out(result[2]));
  PLA #(.in_width(12), .out_width(1), .\table ("0xxx0xxxxxx1 1\n0xxx1xxxxx1x 1\n1xxx0xxxx1xx 1\n1xxx1xxx1xxx 1")) pla_5 (
    .in({RD1, RD2, LOp}), .out(result[3]));
endmodule

module RegisterFile (
  input  EnableWrite,
  input  [2:0] Write,
  input  [7:0] WriteData,
  input  [2:0] PortA,
  input  [2:0] PortB,
  input  clk,
  input  R,
  output [7:0] RD1,
  output [7:0] RD2,
  output [7:0] RD3,
  output [7:0] R6_out,
  output [7:0] R5_out,
  output [7:0] R4_out,
  output [7:0] R3_out,
  output [7:0] R2_out,
  output [7:0] R1_out,
  output [7:0] R0_out
);

  wire decoder_1_out1, decoder_1_out2, decoder_1_out3, decoder_1_out4, decoder_1_out5, decoder_1_out6,
       decoder_1_out7, decoder_2_out0, decoder_2_out1, decoder_2_out2, decoder_2_out3, decoder_2_out4,
       decoder_2_out5, decoder_2_out6, decoder_2_out7, decoder_3_out0, decoder_3_out1, decoder_3_out2,
       decoder_3_out3, decoder_3_out4, decoder_3_out5, decoder_3_out6, decoder_3_out7;

  Decoder #(.select(3)) decoder_1 (
    .out1(decoder_1_out1), .out2(decoder_1_out2), .out3(decoder_1_out3), .out4(decoder_1_out4),
    .out5(decoder_1_out5), .out6(decoder_1_out6), .out7(decoder_1_out7), .sel(Write), .en(EnableWrite));  // open: out0
  LedBar ledbar_1 (
    .led0(WriteData[7]), .led1(WriteData[6]), .led2(WriteData[5]), .led3(WriteData[4]), .led4(WriteData[3]),
    .led5(WriteData[2]), .led6(WriteData[1]), .led7(WriteData[0]));
  Register R6 (.D(WriteData), .en(decoder_1_out7), .clk(clk), .Q(R6_out), .clr(R));
  Register R5 (.D(WriteData), .en(decoder_1_out6), .clk(clk), .Q(R5_out), .clr(R));
  Register R4 (.D(WriteData), .en(decoder_1_out5), .clk(clk), .Q(R4_out), .clr(R));
  Register R3 (.D(WriteData), .en(decoder_1_out4), .clk(clk), .Q(R3_out), .clr(R));
  Register R2 (.D(WriteData), .en(decoder_1_out3), .clk(clk), .Q(R2_out), .clr(R));
  Register R1 (.D(WriteData), .en(decoder_1_out2), .clk(clk), .Q(R1_out), .clr(R));
  Register R0 (.D(WriteData), .en(decoder_1_out1), .clk(clk), .Q(R0_out), .clr(R));
  Decoder #(.enable("false"), .select(3)) decoder_2 (
    .out0(decoder_2_out0), .out1(decoder_2_out1), .out2(decoder_2_out2), .out3(decoder_2_out3),
    .out4(decoder_2_out4), .out5(decoder_2_out5), .out6(decoder_2_out6), .out7(decoder_2_out7), .sel(PortA));
  assign RD1 = decoder_2_out6 ? R5_out : 8'bz;  // Controlled_Buffer controlled_buffer_1
  assign RD1 = decoder_2_out5 ? R4_out : 8'bz;  // Controlled_Buffer controlled_buffer_2
  assign RD1 = decoder_2_out3 ? R2_out : 8'bz;  // Controlled_Buffer controlled_buffer_3
  assign RD1 = decoder_2_out2 ? R1_out : 8'bz;  // Controlled_Buffer controlled_buffer_4
  Decoder #(.enable("false"), .select(3)) decoder_3 (
    .out0(decoder_3_out0), .out1(decoder_3_out1), .out2(decoder_3_out2), .out3(decoder_3_out3),
    .out4(decoder_3_out4), .out5(decoder_3_out5), .out6(decoder_3_out6), .out7(decoder_3_out7), .sel(PortB));
  assign RD1 = decoder_2_out7 ? R6_out : 8'bz;  // Controlled_Buffer controlled_buffer_5
  assign RD1 = decoder_2_out4 ? R3_out : 8'bz;  // Controlled_Buffer controlled_buffer_6
  assign RD1 = decoder_2_out1 ? R0_out : 8'bz;  // Controlled_Buffer controlled_buffer_7
  assign RD1 = decoder_2_out0 ? {8{1'b0}} : 8'bz;  // Controlled_Buffer controlled_buffer_8
  LedBar ledbar_2 (
    .led0(RD1[7]), .led1(RD1[6]), .led2(RD1[5]), .led3(RD1[4]), .led4(RD1[3]), .led5(RD1[2]), .led6(RD1[1]),
    .led7(RD1[0]));
  assign RD2 = decoder_3_out7 ? R6_out : 8'bz;  // Controlled_Buffer controlled_buffer_9
  assign RD2 = decoder_3_out6 ? R5_out : 8'bz;  // Controlled_Buffer controlled_buffer_10
  assign RD2 = decoder_3_out5 ? R4_out : 8'bz;  // Controlled_Buffer controlled_buffer_11
  assign RD2 = decoder_3_out4 ? R3_out : 8'bz;  // Controlled_Buffer controlled_buffer_12
  assign RD2 = decoder_3_out3 ? R2_out : 8'bz;  // Controlled_Buffer controlled_buffer_13
  assign RD2 = decoder_3_out2 ? R1_out : 8'bz;  // Controlled_Buffer controlled_buffer_14
  assign RD2 = decoder_3_out1 ? R0_out : 8'bz;  // Controlled_Buffer controlled_buffer_15
  assign RD2 = decoder_3_out0 ? {8{1'b0}} : 8'bz;  // Controlled_Buffer controlled_buffer_16
  LedBar ledbar_3 (
    .led0(RD2[7]), .led1(RD2[6]), .led2(RD2[5]), .led3(RD2[4]), .led4(RD2[3]), .led5(RD2[2]), .led6(RD2[1]),
    .led7(RD2[0]));
  assign RD3 = decoder_3_out6 ? R6_out : 8'bz;  // Controlled_Buffer controlled_buffer_17
  assign RD3 = decoder_3_out5 ? R5_out : 8'bz;  // Controlled_Buffer controlled_buffer_18
  assign RD3 = decoder_3_out4 ? R4_out : 8'bz;  // Controlled_Buffer controlled_buffer_19
  assign RD3 = decoder_3_out3 ? R3_out : 8'bz;  // Controlled_Buffer controlled_buffer_20
  assign RD3 = decoder_3_out2 ? R2_out : 8'bz;  // Controlled_Buffer controlled_buffer_21
  assign RD3 = decoder_3_out1 ? R1_out : 8'bz;  // Controlled_Buffer controlled_buffer_22
  assign RD3 = decoder_3_out0 ? R0_out : 8'bz;  // Controlled_Buffer controlled_buffer_23
  assign RD3 = decoder_3_out7 ? {8{1'b0}} : 8'bz;  // Controlled_Buffer controlled_buffer_24
  LedBar ledbar_4 (
    .led0(RD3[7]), .led1(RD3[6]), .led2(RD3[5]), .led3(RD3[4]), .led4(RD3[3]), .led5(RD3[2]), .led6(RD3[1]),
    .led7(RD3[0]));

  // Other names for the same wires on the sheet: EnWr = EnableWrite; R0[7:0] = R0_out; R1[7:0] = R1_out;
  //   R2[7:0] = R2_out; R3[7:0] = R3_out; R4[7:0] = R4_out; R5[7:0] = R5_out; R6[7:0] = R6_out
endmodule

module ALU (
  input  [4:0] AluOp,
  input  Enable,
  input  [7:0] RD1,
  input  [7:0] RD2,
  input  clk,
  input  R,
  output [7:0] Result
);

  wire adder_1_cout, ALU_A_Sign, ALU_B_Sign, ALU_Carry, ALU_Carry_IN, ALU_OverFlow, ALU_Zero, and_1_out,
       CondMatch, Flags_Carry, Flags_OutSign, Flags_Overflow, flags_swap, Flags_Zero, multiplexer_3_out,
       nor_1_out, nor_2_out, xor_1_out, xor_2_out;
  wire [1:0] COp, SOp;
  wire [3:0] LOp, multiplexer_2_out;
  wire [6:0] multiplexer_1_out, pla_decoder_lop_1_result;
  wire [7:0] ALU, bit_extender_1_out;

  LedBar #(.matrixcols(5)) ledbar_1 (
    .led0(AluOp[4]), .led1(AluOp[3]), .led2(AluOp[2]), .led3(AluOp[1]), .led4(AluOp[0]));
  PLA #(.in_width(6), .out_width(8), .\table ("000000 00011010\n000001 00011010\n000010 11011010\n000011 11011010\n000100 01010101\n000101 01010101\n000110 11010101\n000111 11010101\n001000 00000011\n001001 00000011\n001010 01000011\n001011 01000011\n001100 00100000\n001101 00100000\n001110 11100000\n001111 11100000\n010000 00110000\n010001 00110000\n010010 11110000\n010011 11110000\n010100 10110000\n010101 10110000\n010110 00000000\n010111 00000000\n011000 00001111\n011001 00001111\n011010 00001000\n011011 00001000\n011100 00001110\n011101 00001110\n011110 00000110\n011111 00000110\n1xxxx0 00001100\n1xxxx1 00001010")) pla_1 (
    .in({AluOp, CondMatch}), .out({COp, SOp, LOp}));
  Multiplexer #(.select(2), .width(8)) multiplexer_1 (
    .in0({8{1'b0}}), .in1(RD1), .in2({RD1[6:0], ALU_Carry_IN}), .in3({ALU_Carry_IN, RD1[7:1]}),
    .out({ALU_A_Sign, multiplexer_1_out}), .sel(SOp));
  LedBar #(.matrixcols(2)) ledbar_2 (.led0(COp[1]), .led1(COp[0]));
  LedBar #(.matrixcols(2)) ledbar_3 (.led0(SOp[1]), .led1(SOp[0]));
  PLA_Decoder_LOp pla_decoder_lop_1 (
    .LOp(LOp), .RD2(RD2[3:0]), .RD1(RD1[3:0]), .Swap(flags_swap), .result(pla_decoder_lop_1_result[3:0]));
  PLA_Decoder_LOp pla_decoder_lop_2 (
    .LOp(LOp), .RD2(RD2[7:4]), .RD1(RD1[7:4]), .result({ALU_B_Sign, pla_decoder_lop_1_result[6:4]}));  // open: Swap
  Multiplexer #(.width(4)) multiplexer_2 (
    .in0({ALU_OverFlow, ALU[7], ALU_Zero, ALU_Carry}), .in1(RD1[3:0]), .out(multiplexer_2_out),
    .sel(flags_swap));
  Register #(.width(4)) Flags (
    .D(multiplexer_2_out), .en(and_1_out), .clk(clk),
    .Q({Flags_Overflow, Flags_OutSign, Flags_Zero, Flags_Carry}), .clr(R));
  and and_1 (and_1_out, Enable, ~AluOp[4]);  // AND_Gate
  LedBar #(.matrixcols(4)) ledbar_4 (.led0(LOp[3]), .led1(LOp[2]), .led2(LOp[1]), .led3(LOp[0]));
  Multiplexer #(.select(2)) multiplexer_3 (
    .in0(ALU_Carry_IN), .in1(ALU_Carry_IN), .in2(1'b0), .in3(1'b0), .out(multiplexer_3_out), .sel(SOp));
  Adder adder_1 (
    .a({ALU_A_Sign, multiplexer_1_out}), .b({ALU_B_Sign, pla_decoder_lop_1_result}), .out(ALU),
    .cin(multiplexer_3_out), .cout(adder_1_cout));
  Multiplexer #(.select(2)) multiplexer_4 (
    .in0(adder_1_cout), .in1(adder_1_cout), .in2(RD1[7]), .in3(RD1[0]), .out(ALU_Carry), .sel(SOp));
  nor nor_1 (nor_1_out, ALU[0], ALU[1], ALU[2], ALU[3]);
  nor nor_2 (nor_2_out, ALU[4], ALU[5], ALU[6], ALU[7]);
  and and_2 (ALU_Zero, nor_1_out, nor_2_out);
  Multiplexer #(.select(2)) multiplexer_5 (
    .in0(1'b0), .in1(1'b1), .in2(RD1[7]), .in3(Flags_Carry), .out(ALU_Carry_IN), .sel(COp));
  xor xor_1 (xor_1_out, ALU[7], ALU_A_Sign);
  xor xor_2 (xor_2_out, ALU[7], ALU_B_Sign);
  and and_3 (ALU_OverFlow, xor_1_out, xor_2_out);
  PLA #(.in_width(8), .out_width(1), .\table ("00000000 0\n00000001 1\n00000010 0\n00000011 1\n00000100 0\n00000101 1\n00000110 0\n00000111 1\n00001000 0\n00001001 1\n00001010 1\n00001011 0\n00001100 0\n00001101 1\n00001110 0\n00001111 1\n00010000 0\n00010001 1\n00010010 0\n00010011 1\n00010100 0\n00010101 1\n00010110 0\n00010111 1\n00011000 1\n00011001 0\n00011010 1\n00011011 0\n00011100 1\n00011101 0\n00011110 1\n00011111 0\n00100000 0\n00100001 1\n00100010 0\n00100011 1\n00100100 0\n00100101 1\n00100110 1\n00100111 0\n00101000 0\n00101001 1\n00101010 1\n00101011 0\n00101100 1\n00101101 0\n00101110 1\n00101111 0\n00110000 0\n00110001 1\n00110010 0\n00110011 1\n00110100 0\n00110101 1\n00110110 1\n00110111 0\n00111000 1\n00111001 0\n00111010 1\n00111011 0\n00111100 0\n00111101 1\n00111110 0\n00111111 1\n01000000 0\n01000001 1\n01000010 0\n01000011 1\n01000100 1\n01000101 0\n01000110 0\n01000111 1\n01001000 0\n01001001 1\n01001010 1\n01001011 0\n01001100 0\n01001101 1\n01001110 1\n01001111 0\n01010000 0\n01010001 1\n01010010 0\n01010011 1\n01010100 1\n01010101 0\n01010110 0\n01010111 1\n01011000 1\n01011001 0\n01011010 1\n01011011 0\n01011100 1\n01011101 0\n01011110 1\n01011111 0\n01100000 0\n01100001 1\n01100010 0\n01100011 1\n01100100 1\n01100101 0\n01100110 1\n01100111 0\n01101000 0\n01101001 1\n01101010 1\n01101011 0\n01101100 1\n01101101 0\n01101110 1\n01101111 0\n01110000 0\n01110001 1\n01110010 0\n01110011 1\n01110100 1\n01110101 0\n01110110 1\n01110111 0\n01111000 1\n01111001 0\n01111010 1\n01111011 0\n01111100 0\n01111101 1\n01111110 1\n01111111 0\n10000000 0\n10000001 1\n10000010 1\n10000011 0\n10000100 0\n10000101 1\n10000110 0\n10000111 1\n10001000 0\n10001001 1\n10001010 0\n10001011 1\n10001100 0\n10001101 1\n10001110 0\n10001111 1\n10010000 0\n10010001 1\n10010010 1\n10010011 0\n10010100 0\n10010101 1\n10010110 0\n10010111 1\n10011000 1\n10011001 0\n10011010 0\n10011011 1\n10011100 1\n10011101 0\n10011110 1\n10011111 0\n10100000 0\n10100001 1\n10100010 1\n10100011 0\n10100100 0\n10100101 1\n10100110 1\n10100111 0\n10101000 0\n10101001 1\n10101010 0\n10101011 1\n10101100 1\n10101101 0\n10101110 1\n10101111 0\n10110000 0\n10110001 1\n10110010 1\n10110011 0\n10110100 0\n10110101 1\n10110110 1\n10110111 0\n10111000 1\n10111001 0\n10111010 0\n10111011 1\n10111100 0\n10111101 1\n10111110 0\n10111111 1\n11000000 0\n11000001 1\n11000010 1\n11000011 0\n11000100 1\n11000101 0\n11000110 0\n11000111 1\n11001000 0\n11001001 1\n11001010 1\n11001011 0\n11001100 0\n11001101 1\n11001110 1\n11001111 0\n11010000 0\n11010001 1\n11010010 1\n11010011 0\n11010100 1\n11010101 0\n11010110 0\n11010111 1\n11011000 1\n11011001 0\n11011010 1\n11011011 0\n11011100 1\n11011101 0\n11011110 1\n11011111 0\n11100000 0\n11100001 1\n11100010 1\n11100011 0\n11100100 1\n11100101 0\n11100110 1\n11100111 0\n11101000 0\n11101001 1\n11101010 1\n11101011 0\n11101100 1\n11101101 0\n11101110 1\n11101111 0\n11110000 0\n11110001 1\n11110010 1\n11110011 0\n11110100 1\n11110101 0\n11110110 1\n11110111 0\n11111000 1\n11111001 0\n11111010 1\n11111011 0\n11111100 0\n11111101 1\n11111110 1\n11111111 0")) pla_2 (
    .in({Flags_Carry, Flags_Zero, Flags_OutSign, Flags_Overflow, AluOp[3:0]}), .out(CondMatch));
  assign bit_extender_1_out = {{4{1'b0}}, {Flags_Overflow, Flags_OutSign, Flags_Zero, Flags_Carry}};  // Bit_Extender bit_extender_1
  Multiplexer #(.width(8)) multiplexer_6 (.in0(ALU), .in1(bit_extender_1_out), .out(Result), .sel(flags_swap));

  // Other names for the same wires on the sheet: FlagsReg[3:0] = {Flags_Overflow, Flags_OutSign, Flags_Zero, Flags_Carry};
  //   ALU_Out_Sign = ALU[7]; writeback_alu = Enable
endmodule

module ProgramCounter (
  input  [7:0] RelativeAddr,
  input  [15:0] AbisoluteAddr,
  input  [1:0] CounterMode,
  input  clk,
  input  Reset,
  output [15:0] PC
);

  wire [15:0] adder_1_out, adder_2_out, bit_extender_1_out, multiplexer_1_out;

  Adder #(.width(16)) adder_1 (.a(PC), .b(16'h2), .out(adder_1_out));  // open: cin, cout
  Adder #(.width(16)) adder_2 (.a(PC), .b(bit_extender_1_out), .out(adder_2_out));  // open: cin, cout
  assign bit_extender_1_out = {{8{RelativeAddr[7]}}, RelativeAddr};  // Bit_Extender bit_extender_1
  Register #(.width(16)) register_1 (.D(multiplexer_1_out), .clk(clk), .Q(PC), .clr(Reset));  // open: en
  Multiplexer #(.select(2), .width(16)) multiplexer_1 (
    .in0(adder_1_out), .in1(adder_2_out), .in2(AbisoluteAddr), .out(multiplexer_1_out), .sel(CounterMode));  // open: in3
endmodule
