// Logisim project temp.circ as structural Verilog: 1 circuit, main circuit sop
module sop (
  input  in0,
  input  in1,
  input  in2,
  input  in3,
  output out0,
  output out1
);

  wire _t0, _t1, _t2, _t3, _t4, _t5, _t6, _t7, and_2_out, and_4_out, and_6_out, and_8_out, and_9_out,
       and_11_out, and_12_out, and_14_out, in0_n, in1_n, in2_n, in3_n, or_1_out, or_2_out, or_3_out, or_4_out;

  not not_1 (in0_n, in0);
  not not_2 (in1_n, in1);
  not not_3 (in2_n, in2);
  not not_4 (in3_n, in3);
  and and_1 (_t0, in0, and_2_out);
  and and_2 (and_2_out, in1_n, in2_n);
  and and_3 (_t1, in0_n, and_4_out);
  and and_4 (and_4_out, in1_n, in2);
  and and_5 (_t2, in0, and_6_out);
  and and_6 (and_6_out, in2_n, in3_n);
  and and_7 (_t3, in0_n, and_8_out);
  and and_8 (and_8_out, in2, in3_n);
  and and_9 (and_9_out, in0_n, in1);
  and and_10 (_t4, and_9_out, and_11_out);
  and and_11 (and_11_out, in2_n, in3);
  and and_12 (and_12_out, in0, in1);
  and and_13 (_t5, and_12_out, and_14_out);
  and and_14 (and_14_out, in2, in3);
  and and_15 (_t6, in1, in3_n);
  and and_16 (_t7, in1_n, in3);
  or or_1 (or_1_out, _t1, _t2);
  or or_2 (or_2_out, _t4, _t5);
  or or_3 (or_3_out, _t0, or_1_out);
  or or_4 (or_4_out, _t3, or_2_out);
  or or_5 (out0, or_3_out, or_4_out);
  or or_6 (out1, _t6, _t7);
endmodule
